// Logisim project 과제3.circ as structural Verilog: 2 circuits, main circuit main
module main (
  input  x,
  input  y,
  input  Clk,
  output S
);

  wire d_ff_1_q, full_adder_1_carry;

  full_adder full_adder_1 (.x(x), .y(y), .Cin(d_ff_1_q), .Sum(S), .Carry(full_adder_1_carry));
  D_Flip_Flop d_ff_1 (.clk(Clk), .D(full_adder_1_carry), .Q(d_ff_1_q));  // open: Qn, preset, en, reset
endmodule

// FA
module full_adder (
  input  x,
  input  y,
  input  Cin,
  output Sum,
  output Carry
);

  wire and_1_out, and_2_out, xor_1_out;

  xor xor_1 (xor_1_out, x, y);
  and and_1 (and_1_out, x, x);
  D_Flip_Flop d_ff_1 ();  // open: clk, D, Q, Qn, preset, en, reset
  xor xor_2 (Sum, xor_1_out, Cin);
  and and_2 (and_2_out, xor_1_out, Cin);
  or or_1 (Carry, and_2_out, and_1_out);
endmodule
